// Logisim project aiAlu.circ as structural Verilog: 1 circuit, main circuit main
module main (
  input  [7:0] in_1,
  input  [7:0] in_2
);

  wire and_2_out, and_3_out, and_4_out, and_5_out, and_6_out, and_7_out, and_8_out;
  wire [0:0] and_1_out;

  and and_1 (and_1_out[0], in_1[0], in_2[0]);
  and and_2 (and_2_out, in_1[1], in_2[1]);
  and and_3 (and_3_out, in_1[2], in_2[2]);
  and and_4 (and_4_out, in_1[3], in_2[3]);
  and and_5 (and_5_out, in_1[4], in_2[4]);
  and and_6 (and_6_out, in_1[5], in_2[5]);
  and and_7 (and_7_out, in_1[6], in_2[6]);
  and and_8 (and_8_out, in_1[7], in_2[7]);
endmodule
